# Fritzing sketch watermeter (saved by Fritzing 0.9.3b)
perfboards: 1

parts:
  U1 = atmega328 [package=dip]
  J1 = Screw terminal - 2 pins [package=THT]  # not connected
  J2 = Screw terminal - 2 pins [package=THT]  # not connected
  J3 = Screw terminal - 2 pins [package=THT]  # not connected
  C1 = Ceramic Capacitor [capacitance=100nF package="100 mil [THT, multilayer]"]
  Serial_Connection = female pin header, 5 pins [form="♀ (female)"]
  LED1 = LED - 5mm [color="Red (633nm)" package="5 mm [THT]"]
  R1 = Resistor [tolerance=±5% resistance=220 package=THT]
  R2 = Resistor [tolerance=±5% resistance=120 package=THT]  # not connected
  R3 = Resistor [tolerance=±5% resistance=22k package=THT]

nets:
  N1: U1.RESET, C1.1
  N2: U1.D0_(RX), Serial_Connection.pin2
  N3: U1.D1_(TX), Serial_Connection.pin3
  N4: U1.VCC, U1.AVCC, Serial_Connection.pin4, R3.Pin_0
  N5: U1.GND, Serial_Connection.pin5, LED1.cathode
  N6: U1.D8, R1.Pin_0
  N7: U1.A0, R3.Pin_1
  N8: C1.0, Serial_Connection.pin1
  N9: LED1.anode, R1.Pin_1

notes:
  USB FTDI / Serial Connection for programming:
  RST - RX - TX - 5V - GND
  On the USB FTDI Adapter connect to:
  DTR - TX - RX - 5V - GND
  Terminal
  5V - GND - S0 - GND - LED - PT
  5V => Power supply
  GND => Common ground
  S0 => S0 Interface
  HOA1405-2
  GND => Cathode + Emitter
  LED => Anode (LED)
  PT => Phototransistor (Collector)
